# Fritzing sketch LTE 4G Connections Sketch (saved by Fritzing 0.9.5d)
breadboards: 1

parts:
  U1 = ESP32-38PinWide [part_number=ESP32-38PinWide]
  Part1 = I2C level shifter bidirectional
  A2 = A7670C LTE modemi dev board
  M1 = RioRand LM2596
  C1 = Capacitor Polarized [part_number=2200uf package=panasonic_g]

nets:
  N1: U1.3.3, Part1.HV
  GND: U1.GND, Part1.GND, A2.Pin_12, M1.Pin_4, C1.-
  N2: U1.GPIO16, Part1.HV2
  N3: U1.GPIO17, Part1.HV1
  N4: Part1.LV, A2.Pin_10
  N5: Part1.LV2, A2.Pin_8
  N6: Part1.LV1, A2.Pin_7
  N7: A2.Pin_11, M1.Pin_3, C1.+

notes:
  LM2596
  Inpult Voltage is 12V DC
  Output Voltage is 3.8V for A7670C
  Use 2200uf Cap for 2Amp Pulse
  A7670C is a low voltage device
  Do not power it with ESP 5V or 3.3V
  Power it using LM2596 and Set its output to 3.8V.
  A7670C module has onboard 1.8V output
  it is necessary to use Logic Level Shifter
  Provide 1.8V out for the Module to LV +
  and GND from Module to GND on Logic Shifter.
  Connect LV1 and LV2 to RXD and TXD of A7670C module
  Connect HV1 and HV2 to TX2 and RX2 of ESP32
  Connect 3.3 V out ESP32 to HV side

custom parts:
  ESP32-38PinWide: Generic 38-Pin ESP32 with wide format (only access to one side of pins on a breadboard) based on Stephen Lilley's HiLetgo ESP-WROOM-32 ESP32 ESP-32S Development Board.
  A7670C LTE modemi dev board: The SIM A7670C 4G + 2G LTE Development Board is a Cat 1 module which supports wireless communication modes of LTE-TDD/LTE-FDD/GSM/GPRS/EDGE.
